# Fritzing sketch smartHouse-model (saved by Fritzing 0.9.3b)
circuit board: 8.46667cm x 5.64444cm
breadboards: 1

parts:
  Part1 = Arduino Uno (Rev3)
  LCD1 = 20x4 LCD display [part_number=2004A]
  LCM1602_IIC1 = LCM1602 IIC [part_number="LCM1602 IIC" chip_label="LCM1602 IIC" package="DIP (Dual Inline) [THT]"]
  TP1 = TTP223 Touch Module [part_number=TTP223]
  TP2 = TTP223 Touch Module [part_number=TTP223]
  TP3 = TTP223 Touch Module [part_number=TTP223]
  M1 = BMP280
  ZS-042_RTC1 = ZS-042 RTC Module

nets:
  N1: Part1.A0, TP1.I/O
  N2: Part1.A1, TP2.I/O
  N3: Part1.A2, TP3.I/O
  N4: Part1.A4/SDA, Part1.A5/SCL, LCM1602_IIC1.SDA, LCM1602_IIC1.SCL, M1.SCL, M1.SDA, ZS-042_RTC1.SDA, ZS-042_RTC1.SCL
  GND: Part1.GND, LCM1602_IIC1.GND, TP1.GND, TP2.GND, TP3.GND, M1.GND, ZS-042_RTC1.GND
  N5: LCD1.Vss, LCM1602_IIC1.K
  N6: LCD1.Vdd, LCM1602_IIC1.A
  N7: LCD1.Vo, LCM1602_IIC1.D7
  N8: LCD1.RS, LCM1602_IIC1.D6
  N9: LCD1.R/W, LCM1602_IIC1.D5
  N10: LCD1.E, LCM1602_IIC1.D4
  N11: LCD1.DB0, LCM1602_IIC1.D3
  N12: LCD1.DB1, LCM1602_IIC1.D2
  N13: LCD1.DB2, LCM1602_IIC1.D1
  N14: LCD1.DB3, LCM1602_IIC1.D0
  N15: LCD1.DB4, LCM1602_IIC1.E
  N16: LCD1.DB5, LCM1602_IIC1.RW
  N17: LCD1.DB6, LCM1602_IIC1.RS
  N18: LCD1.DB7, LCM1602_IIC1.V0
  N19: LCD1.A_+, LCM1602_IIC1.VDD
  N20: LCD1.K_-, LCM1602_IIC1.VSS
  VCC: LCM1602_IIC1.VCC, TP1.VCC, TP2.VCC, TP3.VCC, M1.VIN, ZS-042_RTC1.VCC
  N21: LCM1602_IIC1.LED_A, LCM1602_IIC1.LED_B

custom parts:
  20x4 LCD display: 20x4 character display. CHECK LED POLARITY BEFORE CONNECTING POWER Some versions of the dispaly have the polarity of the LED pins "A" and "K" reversed.
  LCM1602 IIC: I2C-Module to use a 1602 or 2004 LCD on with the wire.h libory Serial LCD Modul
  TTP223 Touch Module: Single touch module. Other side has "A" "B" terminal to short and use "AHLB" & "Toggle" Mode.
  BMP280: Temperature Humidity Barometric presure Sensor, I2C
